// Logisim project cpu.circ as structural Verilog: 4 circuits, main circuit main
module main (
);

  wire and_1_out, and_2_out, and_3_out, clock_1_out, cnd_1_outbool, decoder_1_out1, decoder_1_out2,
       decoder_1_out3, decoder_1_out4, decoder_1_out5, decoder_1_out6, decoder_1_out7, decoder_1_out8,
       decoder_1_out9, decoder_1_out10, decoder_1_out11, decoder_1_out12, multiplexer_4_out,
       multiplexer_7_out, multiplexer_9_out, multiplexer_10_out, multiplexer_12_out, multiplexer_13_out,
       not_1_out, or_1_out, RESET_out;
  wire [1:0] multiplexer_1_out, register_1_q;
  wire [5:0] rom_1_data_2;
  wire [9:0] adder_1_out, callstack_1_out_val, multiplexer_2_out, multiplexer_3_out, register_2_q,
       rom_1_data, rom_1_data_3;
  wire [13:0] multiplexer_5_out, multiplexer_6_out;
  wire [15:0] alu_1_a_out, multiplexer_8_out, multiplexer_11_out, ram_1_dout, register_3_q;
  wire [35:26] rom_1_data_4;

  Clock clock_1 (.out(clock_1_out));
  Register #(.trigger("falling"), .width(2)) register_1 (
    .D(multiplexer_1_out), .en(1'b1), .clk(clock_1_out), .Q(register_1_q), .clr(RESET_out));
  Button RESET (.out(RESET_out));
  Hex_Digit_Display hex_digit_display_1 (.value({2'b00, register_1_q}));  // open: dp
  Register #(.trigger("falling"), .width(10)) register_2 (
    .D(multiplexer_2_out), .en(multiplexer_4_out), .clk(clock_1_out), .Q(register_2_q), .clr(RESET_out));
  Multiplexer #(.select(2), .width(2)) multiplexer_1 (
    .in0(2'b01), .in1(2'b10), .in2(2'b00), .in3(2'b00), .out(multiplexer_1_out), .sel(register_1_q));
  ROM #(.addrWidth(10), .dataWidth(36)) rom_1 (
    .addr(register_2_q), .data({rom_1_data_4, rom_1_data_3, rom_1_data_2, rom_1_data}));
  Adder #(.width(10)) adder_1 (.a(10'h1), .b(register_2_q), .out(adder_1_out));  // open: cin, cout
  Multiplexer #(.select(4), .width(10)) multiplexer_2 (
    .in0(adder_1_out), .in1(adder_1_out), .in2(adder_1_out), .in3(adder_1_out), .in4(adder_1_out),
    .in5(adder_1_out), .in6(adder_1_out), .in7(adder_1_out), .in8(adder_1_out), .in9(adder_1_out),
    .in10(adder_1_out), .in11(adder_1_out), .in12(adder_1_out), .in13(multiplexer_3_out),
    .in14(rom_1_data_3), .in15(callstack_1_out_val), .out(multiplexer_2_out), .sel(rom_1_data_4[35:32]));
  Multiplexer #(.width(10)) multiplexer_3 (
    .in0(adder_1_out), .in1(rom_1_data), .out(multiplexer_3_out), .sel(multiplexer_7_out));
  Multiplexer #(.select(2)) multiplexer_4 (
    .in0(1'b0), .in1(1'b0), .in2(1'b1), .in3(1'b0), .out(multiplexer_4_out), .sel(register_1_q));
  CND cnd_1 (.VALUE(ram_1_dout), .FLAG(rom_1_data_3[2:0]), .OUTBOOL(cnd_1_outbool));
  Multiplexer #(.select(2), .width(14)) multiplexer_5 (
    .in0({rom_1_data_4[29:26], rom_1_data_3}), .in1(multiplexer_6_out),
    .in2({rom_1_data_4[29:26], rom_1_data_3}), .in3({14{1'b0}}), .out(multiplexer_5_out), .sel(register_1_q));
  Multiplexer #(.select(4), .width(14)) multiplexer_6 (
    .in0({rom_1_data_2[3:0], rom_1_data}), .in1({rom_1_data_2[3:0], rom_1_data}),
    .in2({rom_1_data_2[3:0], rom_1_data}), .in3({rom_1_data_2[3:0], rom_1_data}),
    .in4({rom_1_data_2[3:0], rom_1_data}), .in5({rom_1_data_2[3:0], rom_1_data}),
    .in6({rom_1_data_2[3:0], rom_1_data}), .in7({rom_1_data_2[3:0], rom_1_data}),
    .in8({rom_1_data_2[3:0], rom_1_data}), .in9({rom_1_data_2[3:0], rom_1_data}),
    .in10({rom_1_data_2[3:0], rom_1_data}), .in11({rom_1_data_2[3:0], rom_1_data}),
    .in12({rom_1_data_2[3:0], rom_1_data}), .in13({14{1'b0}}), .in14({14{1'b0}}), .in15({14{1'b0}}),
    .out(multiplexer_6_out), .sel(rom_1_data_4[35:32]));
  Decoder #(.select(4)) decoder_1 (
    .out1(decoder_1_out1), .out2(decoder_1_out2), .out3(decoder_1_out3), .out4(decoder_1_out4),
    .out5(decoder_1_out5), .out6(decoder_1_out6), .out7(decoder_1_out7), .out8(decoder_1_out8),
    .out9(decoder_1_out9), .out10(decoder_1_out10), .out11(decoder_1_out11), .out12(decoder_1_out12),
    .sel(rom_1_data_4[35:32]), .en(1'b1));  // open: out0, out13, out14, out15
  Multiplexer #(.select(4)) multiplexer_7 (
    .in0(1'b0), .in1(1'b0), .in2(1'b0), .in3(1'b0), .in4(1'b0), .in5(1'b0), .in6(1'b0), .in7(1'b0),
    .in8(1'b0), .in9(1'b0), .in10(1'b0), .in11(1'b0), .in12(1'b0), .in13(cnd_1_outbool), .in14(1'b0),
    .in15(1'b0), .out(multiplexer_7_out), .sel(rom_1_data_4[35:32]));
  or or_1 (or_1_out, decoder_1_out1, decoder_1_out2, decoder_1_out3, decoder_1_out4, decoder_1_out5, decoder_1_out6, decoder_1_out7, decoder_1_out8, decoder_1_out9, decoder_1_out10, decoder_1_out11, decoder_1_out12);
  and and_1 (and_1_out, or_1_out, multiplexer_4_out);
  Multiplexer #(.select(2), .width(16)) multiplexer_8 (
    .in0({16{1'b0}}), .in1({16{1'b0}}), .in2(alu_1_a_out), .in3({16{1'b0}}), .out(multiplexer_8_out),
    .sel(register_1_q));
  Multiplexer #(.select(4)) multiplexer_9 (
    .in0(1'b0), .in1(1'b0), .in2(1'b0), .in3(1'b0), .in4(1'b0), .in5(1'b0), .in6(1'b0), .in7(1'b0),
    .in8(1'b0), .in9(1'b0), .in10(1'b0), .in11(1'b0), .in12(1'b0), .in13(1'b0), .in14(1'b1), .in15(1'b0),
    .out(multiplexer_9_out), .sel(rom_1_data_4[35:32]));
  Multiplexer #(.select(4)) multiplexer_10 (
    .in0(1'b0), .in1(1'b0), .in2(1'b0), .in3(1'b0), .in4(1'b0), .in5(1'b0), .in6(1'b0), .in7(1'b0),
    .in8(1'b0), .in9(1'b0), .in10(1'b0), .in11(1'b0), .in12(1'b0), .in13(1'b0), .in14(1'b0), .in15(1'b1),
    .out(multiplexer_10_out), .sel(rom_1_data_4[35:32]));
  Multiplexer #(.select(4), .width(16)) multiplexer_11 (
    .in0({16{1'b0}}), .in1(multiplexer_8_out), .in2(multiplexer_8_out), .in3(multiplexer_8_out),
    .in4(multiplexer_8_out), .in5(multiplexer_8_out), .in6(multiplexer_8_out), .in7(multiplexer_8_out),
    .in8(multiplexer_8_out), .in9(multiplexer_8_out), .in10(multiplexer_8_out),
    .in11({rom_1_data_2, rom_1_data}), .in12(ram_1_dout), .in13({16{1'b0}}), .in14({16{1'b0}}),
    .in15({16{1'b0}}), .out(multiplexer_11_out), .sel(rom_1_data_4[35:32]));
  and and_2 (and_2_out, multiplexer_10_out, multiplexer_12_out);
  Multiplexer #(.select(2)) multiplexer_12 (
    .in0(1'b0), .in1(1'b1), .in2(1'b0), .in3(1'b0), .out(multiplexer_12_out), .sel(register_1_q));
  and and_3 (and_3_out, multiplexer_9_out, multiplexer_12_out);
  not not_1 (not_1_out, and_2_out);
  RAM #(.addrWidth(14), .dataWidth(16)) ram_1 (
    .addr(multiplexer_5_out), .we(and_1_out), .oe(1'b1), .clk(clock_1_out), .din(multiplexer_11_out),
    .dout(ram_1_dout));
  ALU alu_1 (.B_IN(ram_1_dout), .A_IN(register_3_q), .INSTRUCTION(rom_1_data_4[35:32]), .A_OUT(alu_1_a_out));
  CALLSTACK callstack_1 (
    .PUSH_VAL(adder_1_out), .PUSH(and_3_out), .POP(and_2_out), .OUT_ENB(not_1_out), .CLOCK(clock_1_out),
    .RESET(RESET_out), .OUT_VAL(callstack_1_out_val));
  Multiplexer #(.select(2)) multiplexer_13 (
    .in0(1'b0), .in1(1'b1), .in2(1'b0), .in3(1'b0), .out(multiplexer_13_out), .sel(register_1_q));
  Register #(.width(16)) register_3 (
    .D(ram_1_dout), .en(multiplexer_13_out), .clk(clock_1_out), .Q(register_3_q), .clr(RESET_out));

  // Notes on the sheet:
  //   contents of rom_1 (hex, n*v repeats v):
  //   b00050004
endmodule

module ALU (
  input  [15:0] B_IN,
  input  [15:0] A_IN,
  input  [3:0] INSTRUCTION,
  output [15:0] A_OUT
);

  wire [15:0] adder_1_out, and_1_out, divider_1_out, divider_1_rem, multiplier_1_out, not_1_out, or_1_out,
       shifter_1_out, subtractor_1_out, xor_1_out;

  Comparator comparator_1 ();  // open: a, b, gt, eq, lt
  Adder #(.width(16)) adder_1 (.a(A_IN), .b(B_IN), .out(adder_1_out));  // open: cin, cout
  Subtractor #(.width(16)) subtractor_1 (.a(A_IN), .b(B_IN), .out(subtractor_1_out));  // open: bin, bout
  Multiplier #(.width(16)) multiplier_1 (.a(A_IN), .b(B_IN), .out(multiplier_1_out));  // open: cin, cout
  Divider #(.width(16)) divider_1 (.a(A_IN), .b(B_IN), .out(divider_1_out), .upper({16{1'b0}}), .rem(divider_1_rem));
  assign not_1_out = ~A_IN;  // NOT_Gate not_1, 16 bits wide
  assign and_1_out = A_IN & B_IN;  // AND_Gate and_1, 16 bits wide
  assign or_1_out = A_IN | B_IN;  // OR_Gate or_1, 16 bits wide
  assign xor_1_out = A_IN ^ B_IN;  // XOR_Gate xor_1, 16 bits wide
  Shifter #(.shift("lr"), .width(16)) shifter_1 (.in(A_IN), .\dist (B_IN[3:0]), .out(shifter_1_out));
  Multiplexer #(.select(4), .width(16)) multiplexer_1 (
    .in0({16{1'b0}}), .in1(adder_1_out), .in2(subtractor_1_out), .in3(multiplier_1_out), .in4(divider_1_out),
    .in5(divider_1_rem), .in6(not_1_out), .in7(and_1_out), .in8(or_1_out), .in9(xor_1_out),
    .in10(shifter_1_out), .in11({16{1'b0}}), .in12({16{1'b0}}), .in13({16{1'b0}}), .in14({16{1'b0}}),
    .in15({16{1'b0}}), .out(A_OUT));  // open: sel
endmodule

module CND (
  input  [15:0] VALUE,
  input  [2:0] FLAG,
  output OUTBOOL
);

  wire not_1_out, not_2_out, not_3_out, not_4_out, or_1_out, or_2_out;

  not not_1 (not_1_out, or_2_out);
  or or_1 (or_1_out, not_1_out, VALUE[15]);
  not not_2 (not_2_out, or_2_out);
  not not_3 (not_3_out, or_1_out);
  or or_2 (or_2_out, VALUE[15], VALUE[14], VALUE[13], VALUE[12], VALUE[11], VALUE[10], VALUE[9], VALUE[8], VALUE[7], VALUE[6], VALUE[5], VALUE[4], VALUE[3], VALUE[2], VALUE[1], VALUE[0]);
  not not_4 (not_4_out, VALUE[15]);
  Multiplexer #(.select(3)) multiplexer_1 (
    .in0(not_2_out), .in1(or_2_out), .in2(not_3_out), .in3(VALUE[15]), .in4(not_4_out), .in5(or_1_out),
    .in6(1'b1), .in7(1'b1), .out(OUTBOOL), .sel(FLAG));
endmodule

module CALLSTACK (
  input  [9:0] PUSH_VAL,
  input  PUSH,
  input  POP,
  input  OUT_ENB,
  input  CLOCK,
  input  RESET,
  output [9:0] OUT_VAL
);

  wire adder_1_cout;
  wire [9:0] adder_1_out, adder_2_out, multiplexer_1_out, multiplexer_2_out, register_1_q;

  Adder #(.width(10)) adder_1 (.a(register_1_q), .b({10{1'b1}}), .out(adder_1_out), .cout(adder_1_cout));  // open: cin
  Multiplexer #(.width(10)) multiplexer_1 (
    .in0({10{1'b0}}), .in1(adder_1_out), .out(multiplexer_1_out), .sel(adder_1_cout));
  Adder #(.width(10)) adder_2 (.a(register_1_q), .b(10'h1), .out(adder_2_out));  // open: cin, cout
  Multiplexer #(.select(2), .width(10)) multiplexer_2 (
    .in0(register_1_q), .in1(multiplexer_1_out), .in2(adder_2_out), .in3(register_1_q),
    .out(multiplexer_2_out), .sel({PUSH, POP}));
  Register #(.width(10)) register_1 (.D(multiplexer_2_out), .en(1'b1), .clk(CLOCK), .Q(register_1_q), .clr(RESET));
  RAM #(.addrWidth(10), .dataWidth(10), .trigger("falling")) stackram (
    .addr(register_1_q), .we(PUSH), .oe(OUT_ENB), .clk(CLOCK), .din(PUSH_VAL), .dout(OUT_VAL));
endmodule
